# Fritzing sketch drone (saved by Fritzing 0.9.3b)
perfboards: 1

parts:
  R3 = Resistor [tolerance=±5% resistance=1k package=THT]
  R1 = Resistor [tolerance=±5% resistance=1k package=THT]
  R2 = Resistor [tolerance=±5% resistance=1k package=THT]
  R4 = Resistor [tolerance=±5% resistance=1.5k package=THT]
  BC547 = NPN-Transistor [package="SOT-23 [SMD]"]
  BC547_2 = NPN-Transistor [package="SOT-23 [SMD]"]
  U1 = ESP8266-12e_smt [part_number=ESP8266-12E]
  Bauteil1 = FTDI Basic Programmer  # not connected
  J1 = Piezo Speaker
  U2 = LIPO-110mAh [package=lipo-110]
  M1 = DC Motor
  M6 = DC Motor
  M2 = DC Motor
  M5 = DC Motor
  M3 = DC Motor
  F3_EVO_Brushed_Flight_Controller1 = F3 EVO Brushed Flight Controller
  M4 = DC Motor

nets:
  N1: R3.Pin_0, U1.GPIO_5
  N2: R1.Pin_0, R2.Pin_1, BC547_2.1
  N3: R1.Pin_1, BC547.0
  N4: R2.Pin_0, R4.Pin_1, F3_EVO_Brushed_Flight_Controller1.+5V_2
  N5: R4.Pin_0, BC547.1, F3_EVO_Brushed_Flight_Controller1.RX2
  N6: BC547.2, BC547_2.2, F3_EVO_Brushed_Flight_Controller1.GND2
  VCC: U1.CH_PD, U1.VCC, F3_EVO_Brushed_Flight_Controller1.3V3
  N7: U1.GND, U1.GPIO_15, F3_EVO_Brushed_Flight_Controller1.GND#76
  N8: J1.pin1, F3_EVO_Brushed_Flight_Controller1.BUZ-
  N9: J1.pin2, F3_EVO_Brushed_Flight_Controller1.BUZ+
  N10: U2.+, F3_EVO_Brushed_Flight_Controller1.VCC
  N11: U2.-, F3_EVO_Brushed_Flight_Controller1.GND#18
  N12: M1.pin_1, F3_EVO_Brushed_Flight_Controller1.M1-
  N13: M1.pin_2, F3_EVO_Brushed_Flight_Controller1.M1+
  N14: M6.pin_1, F3_EVO_Brushed_Flight_Controller1.M6_-
  N15: M6.pin_2, F3_EVO_Brushed_Flight_Controller1.M6_+
  N16: M2.pin_1, F3_EVO_Brushed_Flight_Controller1.M2-
  N17: M2.pin_2, F3_EVO_Brushed_Flight_Controller1.M2+
  N18: M5.pin_1, F3_EVO_Brushed_Flight_Controller1.M5+
  N19: M5.pin_2, F3_EVO_Brushed_Flight_Controller1.M5-
  N20: M3.pin_1, F3_EVO_Brushed_Flight_Controller1.M3+
  N21: M3.pin_2, F3_EVO_Brushed_Flight_Controller1.M3-
  N22: F3_EVO_Brushed_Flight_Controller1.M4+, M4.pin_1
  N23: F3_EVO_Brushed_Flight_Controller1.M4-, M4.pin_2

custom parts:
  ESP8266-12e_smt: These are the first series of modules made with the ESP8266 by the third-party manufacturer AI-Thinker and remain the most widely available. They are collectively referred to as "ESP-xx modules" and to form a workable development system require additional components, especially a serial TTL-to-USB adapter (sometimes called a USB-to-UART bridge) and an external 3.3V power supply. ESP8266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
  F3 EVO Brushed Flight Controller: The Hyperion F3 EVO Brushed Flight Controller gives you all the features in a small size and designed for micro size quads with brushed motors. Dedicated Open source Cleanflight software ensures that you are always updated. Description: Brand Name: Hyperion Item Name: F3 EVO Brushed Flight Controller Dimension: 22mm*32.5mm Thickness: 1.2mm Weight: 3g Features: 1. F3_EVO_Brush is in the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
